# Fritzing sketch controller (saved by Fritzing 0.7.7b)
breadboards: 1

parts:
  Teensy1 = Teensy 2.0
  VCC1 = 4 x AAA Battery Mount
  Q1 = PNP-Transistor [package="TO92 [THT]"]
  R1 = 390 Ω Resistor [package=THT]
  Q2 = PNP-Transistor [package="TO92 [THT]"]
  R2 = 390 Ω Resistor [package=THT]
  M1 = DC Motor
  LED1 = LED - 5mm [color="Red (633nm)" package="5 mm [THT]"]
  S1 = Pushbutton [package=THT]
  R3 = Photocell (LDR) [package=THT]

nets:
  N1: Teensy1.GND, VCC1.-, M1.pin_1, LED1.cathode, S1.leg0, R3.pin_1
  N2: Teensy1.D2, S1.leg1
  N3: Teensy1.F7, R2.Pin_0
  N4: Teensy1.F6, R1.Pin_0
  N5: Teensy1.F1, R3.pin_0
  N6: VCC1.+, Q1.E, Q2.E
  N7: Q1.B, R1.Pin_1
  N8: Q1.C, M1.pin_2
  N9: Q2.B, R2.Pin_1
  N10: Q2.C, LED1.anode

custom parts:
  390 Ω Resistor: A generic resistor (0.25W)
